// Logisim project chapter2.circ as structural Verilog
module HalfAdder (
  input  a,
  input  b,
  output sum,
  output carry
);

  xor xor_1 (sum, b, a);
  and and_1 (carry, b, a);
endmodule

module FullAdder (
  input  c,
  input  b,
  input  a,
  output sum,
  output carry
);

  wire halfadder_1_carry, halfadder_1_sum, not_1_out, or_1_out, xor_1_out;

  HalfAdder halfadder_1 (.a(b), .b(c), .sum(halfadder_1_sum), .carry(halfadder_1_carry));
  xor xor_1 (xor_1_out, b, c);
  or or_1 (or_1_out, c, b);
  not not_1 (not_1_out, xor_1_out);
  Multiplexer #(.enable("false")) multiplexer_1 (.in0(halfadder_1_sum), .in1(not_1_out), .out(sum), .sel(a));
  Multiplexer #(.enable("false")) multiplexer_2 (.in0(halfadder_1_carry), .in1(or_1_out), .out(carry), .sel(a));

  // Notes on the sheet:
  //   xorBC
  //   sumBC
  //   carryBC
  //   orBC
  //   notxorbc
endmodule

module Add16 (
  input  [15:0] in_1,
  input  [15:0] in_2,
  output [15:0] out_3
);

  wire fulladder_1_carry, fulladder_2_carry, fulladder_3_carry, fulladder_4_carry, fulladder_5_carry,
       fulladder_6_carry, fulladder_7_carry, fulladder_8_carry, fulladder_9_carry, fulladder_10_carry,
       fulladder_11_carry, fulladder_12_carry, fulladder_13_carry, fulladder_14_carry, halfadder_1_carry;

  HalfAdder halfadder_1 (.a(in_1[0]), .b(in_2[0]), .sum(out_3[0]), .carry(halfadder_1_carry));
  FullAdder fulladder_1 (.c(halfadder_1_carry), .b(in_1[1]), .a(in_2[1]), .sum(out_3[1]), .carry(fulladder_1_carry));
  FullAdder fulladder_2 (.c(fulladder_1_carry), .b(in_1[2]), .a(in_2[2]), .sum(out_3[2]), .carry(fulladder_2_carry));
  FullAdder fulladder_3 (.c(fulladder_2_carry), .b(in_1[3]), .a(in_2[3]), .sum(out_3[3]), .carry(fulladder_3_carry));
  FullAdder fulladder_4 (.c(fulladder_3_carry), .b(in_1[4]), .a(in_2[4]), .sum(out_3[4]), .carry(fulladder_4_carry));
  FullAdder fulladder_5 (.c(fulladder_4_carry), .b(in_1[5]), .a(in_2[5]), .sum(out_3[5]), .carry(fulladder_5_carry));
  FullAdder fulladder_6 (.c(fulladder_5_carry), .b(in_1[6]), .a(in_2[6]), .sum(out_3[6]), .carry(fulladder_6_carry));
  FullAdder fulladder_7 (.c(fulladder_6_carry), .b(in_1[7]), .a(in_2[7]), .sum(out_3[7]), .carry(fulladder_7_carry));
  FullAdder fulladder_8 (.c(fulladder_7_carry), .b(in_1[8]), .a(in_2[8]), .sum(out_3[8]), .carry(fulladder_8_carry));
  FullAdder fulladder_9 (.c(fulladder_8_carry), .b(in_1[9]), .a(in_2[9]), .sum(out_3[9]), .carry(fulladder_9_carry));
  FullAdder fulladder_10 (
    .c(fulladder_9_carry), .b(in_1[10]), .a(in_2[10]), .sum(out_3[10]), .carry(fulladder_10_carry));
  FullAdder fulladder_11 (
    .c(fulladder_10_carry), .b(in_1[11]), .a(in_2[11]), .sum(out_3[11]), .carry(fulladder_11_carry));
  FullAdder fulladder_12 (
    .c(fulladder_11_carry), .b(in_1[12]), .a(in_2[12]), .sum(out_3[12]), .carry(fulladder_12_carry));
  FullAdder fulladder_13 (
    .c(fulladder_12_carry), .b(in_1[13]), .a(in_2[13]), .sum(out_3[13]), .carry(fulladder_13_carry));
  FullAdder fulladder_14 (
    .c(fulladder_13_carry), .b(in_1[14]), .a(in_2[14]), .sum(out_3[14]), .carry(fulladder_14_carry));
  FullAdder fulladder_15 (.c(fulladder_14_carry), .b(in_1[15]), .a(in_2[15]), .sum(out_3[15]));  // open: carry
endmodule
