// Logisim project chapter3.circ as structural Verilog
module Bit (
  input  load,
  input  in,
  output out
);

  wire clock_1_out, multiplexer_1_out;

  Clock clock_1 (.out(clock_1_out));
  Multiplexer #(.enable("false")) multiplexer_1 (.in0(out), .in1(in), .out(multiplexer_1_out), .sel(load));
  D_Flip_Flop #(.trigger("falling")) d_ff_1 (
    .clk(clock_1_out), .D(multiplexer_1_out), .Q(out));  // open: Qn, preset, en, reset
endmodule

module Register (
  input  [15:0] in,
  input  load,
  output [15:0] out
);

  wire clock_1_out;

  Clock clock_1 (.out(clock_1_out));
  Register_part #(.width(1)) register_1 (.D(in[0]), .en(load), .Q(out[0]), .clk(clock_1_out));  // open: clr
  Register_part #(.width(1)) register_2 (.D(in[1]), .en(load), .Q(out[1]), .clk(clock_1_out));  // open: clr
  Register_part #(.width(1)) register_3 (.D(in[2]), .en(load), .Q(out[2]), .clk(clock_1_out));  // open: clr
  Register_part #(.width(1)) register_4 (.D(in[3]), .en(load), .Q(out[3]), .clk(clock_1_out));  // open: clr
  Register_part #(.width(1)) register_5 (.D(in[12]), .en(load), .Q(out[12]), .clk(clock_1_out));  // open: clr
  Register_part #(.width(1)) register_6 (.D(in[13]), .en(load), .Q(out[13]), .clk(clock_1_out));  // open: clr
  Register_part #(.width(1)) register_7 (.D(in[14]), .en(load), .Q(out[14]), .clk(clock_1_out));  // open: clr
  Register_part #(.width(1)) register_8 (.D(in[15]), .en(load), .Q(out[15]), .clk(clock_1_out));  // open: clr
  Register_part #(.width(1)) register_9 (.D(in[4]), .en(load), .Q(out[4]), .clk(clock_1_out));  // open: clr
  Register_part #(.width(1)) register_10 (.D(in[5]), .en(load), .Q(out[5]), .clk(clock_1_out));  // open: clr
  Register_part #(.width(1)) register_11 (.D(in[6]), .en(load), .Q(out[6]), .clk(clock_1_out));  // open: clr
  Register_part #(.width(1)) register_12 (.D(in[7]), .en(load), .Q(out[7]), .clk(clock_1_out));  // open: clr
  Register_part #(.width(1)) register_13 (.D(in[8]), .en(load), .Q(out[8]), .clk(clock_1_out));  // open: clr
  Register_part #(.width(1)) register_14 (.D(in[9]), .en(load), .Q(out[9]), .clk(clock_1_out));  // open: clr
  Register_part #(.width(1)) register_15 (.D(in[10]), .en(load), .Q(out[10]), .clk(clock_1_out));  // open: clr
  Register_part #(.width(1)) register_16 (.D(in[11]), .en(load), .Q(out[11]), .clk(clock_1_out));  // open: clr
endmodule
